// Logisim project 32clas.circ as structural Verilog
module main (
  input  in_1,
  input  [31:0] A_i,
  input  [31:0] B_i,
  input  mode_i,
  input  [1:0] vecSize_i,
  output [31:0] S_o,
  output out_7
);

  wire carry_generator_1_c, carry_generator_1_cout, carry_generator_2_c, carry_generator_2_cout,
       carry_generator_3_c, carry_generator_3_cout, carry_generator_4_c, propagation_generator_1_g,
       propagation_generator_1_p, propagation_generator_2_g, propagation_generator_2_p,
       propagation_generator_3_g, propagation_generator_3_p, propagation_generator_4_g,
       propagation_generator_4_p, propagation_generator_5_g, propagation_generator_5_p,
       propagation_generator_6_g, propagation_generator_6_p, propagation_generator_7_g,
       propagation_generator_7_p, propagation_generator_8_g, propagation_generator_8_p;
  wire [3:0] lookahead4bit_1_s, lookahead4bit_2_s, lookahead4bit_3_s, lookahead4bit_4_s, lookahead4bit_5_s,
       lookahead4bit_6_s, lookahead4bit_7_s, lookahead4bit_8_s, propagation_generator_1_vec_g,
       propagation_generator_1_vec_p, propagation_generator_2_vec_g, propagation_generator_2_vec_p,
       propagation_generator_3_vec_g, propagation_generator_3_vec_p, propagation_generator_4_vec_g,
       propagation_generator_4_vec_p, propagation_generator_5_vec_g, propagation_generator_5_vec_p,
       propagation_generator_6_vec_g, propagation_generator_6_vec_p, propagation_generator_7_vec_g,
       propagation_generator_7_vec_p, propagation_generator_8_vec_g, propagation_generator_8_vec_p,
       signal_decoder_1_a0, signal_decoder_1_a1, signal_decoder_1_a2, signal_decoder_1_a3,
       signal_decoder_1_a4, signal_decoder_1_a5, signal_decoder_1_a6, signal_decoder_1_a7,
       signal_decoder_1_b0, signal_decoder_1_b1, signal_decoder_1_b2, signal_decoder_1_b3,
       signal_decoder_1_b4, signal_decoder_1_b5, signal_decoder_1_b6, signal_decoder_1_b7;
  wire [31:0] inverter_1_s;

  inverter inverter_1 (.a(B_i), .sel(mode_i), .s(inverter_1_s));
  signal_decoder signal_decoder_1 (
    .a(A_i), .b(inverter_1_s), .a0(signal_decoder_1_a0), .a1(signal_decoder_1_a1), .a2(signal_decoder_1_a2),
    .a3(signal_decoder_1_a3), .a4(signal_decoder_1_a4), .a5(signal_decoder_1_a5), .a6(signal_decoder_1_a6),
    .a7(signal_decoder_1_a7), .b0(signal_decoder_1_b0), .b1(signal_decoder_1_b1), .b2(signal_decoder_1_b2),
    .b3(signal_decoder_1_b3), .b4(signal_decoder_1_b4), .b5(signal_decoder_1_b5), .b6(signal_decoder_1_b6),
    .b7(signal_decoder_1_b7));
  propagation_generator propagation_generator_1 (
    .a(signal_decoder_1_a4), .b(signal_decoder_1_b4), .vec_p(propagation_generator_1_vec_p),
    .vec_g(propagation_generator_1_vec_g), .p(propagation_generator_1_p), .g(propagation_generator_1_g));
  propagation_generator propagation_generator_2 (
    .a(signal_decoder_1_a5), .b(signal_decoder_1_b5), .vec_p(propagation_generator_2_vec_p),
    .vec_g(propagation_generator_2_vec_g), .p(propagation_generator_2_p), .g(propagation_generator_2_g));
  propagation_generator propagation_generator_3 (
    .a(signal_decoder_1_a6), .b(signal_decoder_1_b6), .vec_p(propagation_generator_3_vec_p),
    .vec_g(propagation_generator_3_vec_g), .p(propagation_generator_3_p), .g(propagation_generator_3_g));
  propagation_generator propagation_generator_4 (
    .a(signal_decoder_1_a7), .b(signal_decoder_1_b7), .vec_p(propagation_generator_4_vec_p),
    .vec_g(propagation_generator_4_vec_g), .p(propagation_generator_4_p), .g(propagation_generator_4_g));
  propagation_generator propagation_generator_5 (
    .a(signal_decoder_1_a0), .b(signal_decoder_1_b0), .vec_p(propagation_generator_5_vec_p),
    .vec_g(propagation_generator_5_vec_g), .p(propagation_generator_5_p), .g(propagation_generator_5_g));
  propagation_generator propagation_generator_6 (
    .a(signal_decoder_1_a1), .b(signal_decoder_1_b1), .vec_p(propagation_generator_6_vec_p),
    .vec_g(propagation_generator_6_vec_g), .p(propagation_generator_6_p), .g(propagation_generator_6_g));
  propagation_generator propagation_generator_7 (
    .a(signal_decoder_1_a2), .b(signal_decoder_1_b2), .vec_p(propagation_generator_7_vec_p),
    .vec_g(propagation_generator_7_vec_g), .p(propagation_generator_7_p), .g(propagation_generator_7_g));
  propagation_generator propagation_generator_8 (
    .a(signal_decoder_1_a3), .b(signal_decoder_1_b3), .vec_p(propagation_generator_8_vec_p),
    .vec_g(propagation_generator_8_vec_g), .p(propagation_generator_8_p), .g(propagation_generator_8_g));
  LookAhead4Bit lookahead4bit_1 (
    .a(signal_decoder_1_a0), .b(signal_decoder_1_b0), .p(propagation_generator_5_vec_p),
    .g(propagation_generator_5_vec_g), .cin(in_1), .s(lookahead4bit_1_s));
  carry_generator carry_generator_1 (
    .p1(propagation_generator_5_p), .g1(propagation_generator_5_g), .p2(propagation_generator_6_p),
    .g2(propagation_generator_6_g), .cin(in_1), .cout(carry_generator_1_cout), .c(carry_generator_1_c));
  LookAhead4Bit lookahead4bit_2 (
    .a(signal_decoder_1_a1), .b(signal_decoder_1_b1), .p(propagation_generator_6_vec_p),
    .g(propagation_generator_6_vec_g), .cin(carry_generator_1_c), .s(lookahead4bit_2_s));
  LookAhead4Bit lookahead4bit_3 (
    .a(signal_decoder_1_a2), .b(signal_decoder_1_b2), .p(propagation_generator_7_vec_p),
    .g(propagation_generator_7_vec_g), .cin(carry_generator_1_cout), .s(lookahead4bit_3_s));
  carry_generator carry_generator_2 (
    .p1(propagation_generator_7_p), .g1(propagation_generator_7_g), .p2(propagation_generator_8_p),
    .g2(propagation_generator_8_g), .cin(carry_generator_1_cout), .cout(carry_generator_2_cout),
    .c(carry_generator_2_c));
  LookAhead4Bit lookahead4bit_4 (
    .a(signal_decoder_1_a3), .b(signal_decoder_1_b3), .p(propagation_generator_8_vec_p),
    .g(propagation_generator_8_vec_g), .cin(carry_generator_2_c), .s(lookahead4bit_4_s));
  LookAhead4Bit lookahead4bit_5 (
    .a(signal_decoder_1_a4), .b(signal_decoder_1_b4), .p(propagation_generator_1_vec_p),
    .g(propagation_generator_1_vec_g), .cin(carry_generator_2_cout), .s(lookahead4bit_5_s));
  carry_generator carry_generator_3 (
    .p1(propagation_generator_1_p), .g1(propagation_generator_1_g), .p2(propagation_generator_2_p),
    .g2(propagation_generator_2_g), .cin(carry_generator_2_cout), .cout(carry_generator_3_cout),
    .c(carry_generator_3_c));
  LookAhead4Bit lookahead4bit_6 (
    .a(signal_decoder_1_a5), .b(signal_decoder_1_b5), .p(propagation_generator_2_vec_p),
    .g(propagation_generator_2_vec_g), .cin(carry_generator_3_c), .s(lookahead4bit_6_s));
  LookAhead4Bit lookahead4bit_7 (
    .a(signal_decoder_1_a6), .b(signal_decoder_1_b6), .p(propagation_generator_3_vec_p),
    .g(propagation_generator_3_vec_g), .cin(carry_generator_3_cout), .s(lookahead4bit_7_s));
  carry_generator carry_generator_4 (
    .p1(propagation_generator_3_p), .g1(propagation_generator_3_g), .p2(propagation_generator_4_p),
    .g2(propagation_generator_4_g), .cin(carry_generator_3_cout), .cout(out_7), .c(carry_generator_4_c));
  LookAhead4Bit lookahead4bit_8 (
    .a(signal_decoder_1_a7), .b(signal_decoder_1_b7), .p(propagation_generator_4_vec_p),
    .g(propagation_generator_4_vec_g), .cin(carry_generator_4_c), .s(lookahead4bit_8_s));
  output_size output_size_1 (
    .s0(lookahead4bit_1_s), .s1(lookahead4bit_2_s), .s2(lookahead4bit_3_s), .s3(lookahead4bit_4_s),
    .s4(lookahead4bit_5_s), .s5(lookahead4bit_6_s), .s6(lookahead4bit_7_s), .s7(lookahead4bit_8_s),
    .sel(vecSize_i), .s(S_o));
endmodule

// VHDL entity inverter, as the project stores it:
LIBRARY ieee;
USE ieee.std_logic_1164.ALL;

ENTITY inverter IS
    PORT (
        a : IN STD_LOGIC_VECTOR(31 DOWNTO 0);
        sel : IN STD_LOGIC;
        s : OUT STD_LOGIC_VECTOR(31 DOWNTO 0)
    );
END inverter;

ARCHITECTURE behavior OF inverter IS
BEGIN
    PROCESS (a, sel)
    BEGIN
        IF (sel = '1') THEN
            s <= NOT a;
        ELSE
            s <= a;
        END IF;
    END PROCESS;
END behavior;

// VHDL entity carry_generator, as the project stores it:
-- CLA generator 4-bit

library ieee;
use ieee.std_logic_1164.all;

ENTITY carry_generator IS
    PORT (
        p1, g1, p2, g2, cin : IN STD_LOGIC;
        cout, c : OUT STD_LOGIC
    );
END carry_generator;

ARCHITECTURE behavior OF carry_generator IS

BEGIN
    c <= g1 OR (p1 AND cin);
    cout <= g2 OR (p2 AND g1) OR (p1 AND g2 AND cin);
END behavior;

// VHDL entity LookAhead4Bit, as the project stores it:
-- LookAhead 4-Bit

LIBRARY ieee;
use ieee.std_logic_1164.all;

ENTITY LookAhead4Bit IS
    PORT(
        a, b, p, g : IN STD_LOGIC_VECTOR(3 DOWNTO 0);
        cin : IN STD_LOGIC;
        s : OUT STD_LOGIC_VECTOR(3 DOWNTO 0)
    );
END LookAhead4Bit;

ARCHITECTURE LookAhead4Bit OF LookAhead4Bit IS
BEGIN
    s(0) <= p(0) XOR cin;
    s(1) <= p(1) XOR (g(0) OR (p(0) AND cin));
    s(2) <= p(2) XOR (g(1) OR (p(1) AND g(0)) OR (p(1) AND p(0) AND cin));
    s(3) <= p(3) XOR ((p(2) AND g(1)) OR (p(2) AND p(1) AND g(0)) OR (p(2) AND p(1) AND p(0) AND cin));
END LookAhead4Bit;

// VHDL entity output_size, as the project stores it:
-- moduling different sizes of adders

LIBRARY ieee;
use ieee.std_logic_1164.ALL;

ENTITY output_size IS
    PORT (
        s0, s1, s2, s3, s4, s5, s6, s7 : IN STD_LOGIC_VECTOR(3 DOWNTO 0);
        sel : IN STD_LOGIC_VECTOR(1 DOWNTO 0);
        s : OUT STD_LOGIC_VECTOR(31 DOWNTO 0)
    );
END output_size;

ARCHITECTURE behavior OF output_size IS
    SIGNAL s_int : STD_LOGIC_VECTOR(31 DOWNTO 0);

BEGIN
    s_int(3 DOWNTO 0) <= s0;
    s_int(7 DOWNTO 4) <= s1;
    s_int(11 DOWNTO 8) <= s2;
    s_int(15 DOWNTO 12) <= s3;
    s_int(19 DOWNTO 16) <= s4;
    s_int(23 DOWNTO 20) <= s5;
    s_int(27 DOWNTO 24) <= s6;
    s_int(31 DOWNTO 28) <= s7;

    PROCESS (sel)
    BEGIN
        CASE sel IS
            WHEN "00" =>
                s(3 DOWNTO 0) <= s_int(3 DOWNTO 0);
                s(31 DOWNTO 4) <=  "0000000000000000000000000000";
            WHEN "01" =>
                s(7 DOWNTO 0) <= s_int(7 DOWNTO 0);
                s(31 DOWNTO 8) <= "000000000000000000000000";
            WHEN "10" =>
                s(15 DOWNTO 0) <= s_int(15 DOWNTO 0);
                s(31 DOWNTO 16) <= "0000000000000000";
            WHEN "11" =>
                s <= s_int;
            WHEN others =>
            	s <= "00000000000000000000000000000000";
        END CASE;
    END PROCESS;
END behavior;

// VHDL entity propagation_generator, as the project stores it:
-- propagation generator for CLA 4-Bit Adder

LIBRARY ieee;
USE ieee.std_logic_1164.ALL;

ENTITY propagation_generator IS
    PORT (
        a, b : IN STD_LOGIC_VECTOR(3 DOWNTO 0);
        vec_p, vec_g : OUT STD_LOGIC_VECTOR(3 DOWNTO 0);
        p, g : OUT STD_LOGIC
    );
END propagation_generator;

ARCHITECTURE behavior OF propagation_generator IS
    SIGNAL p_vec, g_vec : STD_LOGIC_VECTOR(3 DOWNTO 0);
BEGIN
    PROCESS (a, b)
    BEGIN
        p_vec <= a XOR b;
        g_vec <= a AND b;
    END PROCESS;

    vec_p <= p_vec;
    vec_g <= g_vec;
    p <= p_vec(3) AND p_vec(2) AND p_vec(1) AND p_vec(0);
    g <= g_vec(3) OR (g_vec(2) AND p_vec(3)) OR (p_vec(3) AND p_vec(2) AND g_vec(1)) OR (p_vec(3) AND p_vec(2) AND p_vec(1) AND g_vec(0));
END behavior;

// VHDL entity signal_decoder, as the project stores it:
LIBRARY ieee;
USE ieee.std_logic_1164.ALL;

ENTITY signal_decoder IS
    PORT (
        a, b : IN STD_LOGIC_VECTOR(31 DOWNTO 0);
        a0, a1, a2, a3, a4, a5, a6, a7, b0, b1, b2, b3, b4, b5, b6, b7 : OUT STD_LOGIC_VECTOR(3 DOWNTO 0)
    );
END signal_decoder;

ARCHITECTURE Behavioral OF signal_decoder IS

BEGIN
    a0 <= a(3 DOWNTO 0);
    a1 <= a(7 DOWNTO 4);
    a2 <= a(11 DOWNTO 8);
    a3 <= a(15 DOWNTO 12);
    a4 <= a(19 DOWNTO 16);
    a5 <= a(23 DOWNTO 20);
    a6 <= a(27 DOWNTO 24);
    a7 <= a(31 DOWNTO 28);

    b0 <= b(3 DOWNTO 0);
    b1 <= b(7 DOWNTO 4);
    b2 <= b(11 DOWNTO 8);
    b3 <= b(15 DOWNTO 12);
    b4 <= b(19 DOWNTO 16);
    b5 <= b(23 DOWNTO 20);
    b6 <= b(27 DOWNTO 24);
    b7 <= b(31 DOWNTO 28);
END Behavioral;
